// Logisim project AC.circ as structural Verilog: 2 circuits, main circuit main
module main (
  input  in_1,
  input  in_2,
  input  in_3
);

  wire c74173_9_q1, c74173_9_q2, c74173_9_q3, c74173_9_q4, c74173_10_q1, c74173_10_q2, c74173_10_q3,
       c74173_10_q4, dipswitch_1_sw1, dipswitch_1_sw2, dipswitch_1_sw3, dipswitch_1_sw4, dipswitch_2_sw5,
       dipswitch_2_sw6, dipswitch_2_sw7, dipswitch_2_sw8, n7402_1_pin1, n7402_1_pin3, n7402_1_pin6,
       n7402_1_pin8, n7402_1_pin10, n7402_2_pin1, n7402_2_pin4, n7402_2_pin10, n7402_2_pin13, n7408_1_pin3,
       n7408_1_pin11, n7408_2_pin11, n74138_1_pin4, n74138_1_pin6, n74138_1_pin7, n74138_1_pin9,
       n74138_1_pin10, n74138_1_pin11, n74138_1_pin12, n74138_1_pin13, n74138_1_pin14, n74138_2_pin4,
       n74138_2_pin6, n74138_2_pin9, n74138_2_pin10, n74138_2_pin11, n74138_2_pin12, n74138_2_pin13,
       n74138_2_pin14, n74157_1_pin4, n74157_1_pin7, n74157_1_pin9, n74157_1_pin12, n74157_2_pin3,
       n74157_2_pin6, n74157_2_pin10, n74157_2_pin13, n74161_1_pin1, n74161_1_pin2, n74161_1_pin7,
       n74161_2_pin11, n74161_2_pin12, n74161_2_pin13, n74161_2_pin14, n74181_1_p1, n74181_1_p4, n74181_1_p8,
       n74181_1_p12, n74181_1_p14, n74181_1_p15, n74181_1_p16, n74181_1_p17, n74181_1_p18, n74181_2_p1,
       n74181_2_p4, n74181_2_p8, n74181_2_p12, n74181_2_p14, n74181_2_p15, n74181_2_p16, n74181_2_p17,
       n74245_1_pin2, n74245_1_pin3, n74245_1_pin4, n74245_1_pin5, n74245_1_pin6, n74245_1_pin7,
       n74245_1_pin8, n74245_1_pin9, n74245_1_pin14, n74245_1_pin15, n74245_1_pin16, n74245_1_pin19,
       n74245_2_pin1, n74245_2_pin2, n74245_2_pin3, n74245_2_pin4, n74245_2_pin5, n74245_2_pin6,
       n74245_2_pin7, n74245_2_pin8, n74245_2_pin9, n74245_4_pin1, n74245_6_pin14, n74245_7_pin1,
       n74245_7_pin2, n74245_7_pin3, n74245_7_pin4, n74245_7_pin5, n74245_7_pin6, n74245_7_pin7,
       n74245_7_pin8, n74245_7_pin9, not_1_out;
  wire [3:0] c74173_7_q1;
  wire [7:0] n74157_2_pin4, ram_1_dout, rom_1_data, rom_2_data;
  wire [10:0] n74161_1_pin14;

  _74161 u_74161_1 (
    .pin1(n74161_1_pin1), .pin2(n74161_1_pin2), .pin7(n74161_1_pin7), .pin14(n74161_1_pin14[0]),
    .pin13(n74161_1_pin14[1]), .pin12(n74161_1_pin14[2]), .pin11(n74161_1_pin14[3]), .pin10(n74161_1_pin7));  // open: pin3, pin4, pin5, pin6, pin15, pin9
  Clock clock_1 (.out(n74161_1_pin2));
  ROM #(.addrWidth(11)) rom_1 (.addr(n74161_1_pin14), .data(rom_1_data));
  ROM #(.addrWidth(11)) rom_2 (.addr(n74161_1_pin14), .data(rom_2_data));
  _7402 u_7402_1 (
    .pin1(n7402_1_pin1), .pin2(rom_1_data[6]), .pin3(n7402_1_pin3), .pin4(n74161_1_pin1),
    .pin5(rom_1_data[7]), .pin6(n7402_1_pin6), .pin10(n7402_1_pin10), .pin9(rom_2_data[4]),
    .pin8(n7402_1_pin8));  // open: pin13, pin12, pin11
  _74245 u_74245_1 (
    .pin2(n74245_1_pin2), .pin3(n74245_1_pin3), .pin4(n74245_1_pin4), .pin5(n74245_1_pin5),
    .pin6(n74245_1_pin6), .pin7(n74245_1_pin7), .pin8(n74245_1_pin8), .pin9(n74245_1_pin9),
    .pin19(n74245_1_pin19), .pin18(n74161_1_pin14[5]), .pin17(n74161_1_pin14[6]), .pin16(n74245_1_pin16),
    .pin15(n74245_1_pin15), .pin14(n74245_1_pin14), .pin13(n74245_1_pin14), .pin12(n74245_1_pin14),
    .pin11(n74245_1_pin14));  // open: pin1
  _74138 u_74138_1 (
    .pin1(rom_1_data[0]), .pin2(rom_1_data[1]), .pin3(rom_1_data[2]), .pin4(n74138_1_pin4),
    .pin5(n74138_1_pin4), .pin6(n74138_1_pin6), .pin7(n74138_1_pin7), .pin14(n74138_1_pin14),
    .pin13(n74138_1_pin13), .pin12(n74138_1_pin12), .pin11(n74138_1_pin11), .pin10(n74138_1_pin10),
    .pin9(n74138_1_pin9));  // open: pin15
  _74138 u_74138_2 (
    .pin1(rom_1_data[3]), .pin2(rom_1_data[4]), .pin3(rom_1_data[5]), .pin4(n74138_2_pin4),
    .pin5(n74138_2_pin4), .pin6(n74138_2_pin6), .pin7(n74245_1_pin19), .pin14(n74138_2_pin14),
    .pin13(n74138_2_pin13), .pin12(n74138_2_pin12), .pin11(n74138_2_pin11), .pin10(n74138_2_pin10),
    .pin9(n74138_2_pin9));  // open: pin15
  c74173 c74173_1 (
    .CLK(n74161_1_pin2), .nG1(n74138_1_pin7), .nG2(n74138_1_pin7), .D2(n74245_1_pin3), .D3(n74245_1_pin4),
    .D4(n74245_1_pin5), .D1(n74245_1_pin2), .Q2(n74161_1_pin14[6]), .Q3(n74245_1_pin16), .Q4(n74245_1_pin15),
    .Q1(n74161_1_pin14[5]));  // open: CLR, M, N
  c74173 c74173_2 (
    .CLK(n74161_1_pin2), .nG1(n74138_1_pin7), .nG2(n74138_1_pin7), .D2(n74245_1_pin7), .D3(n74245_1_pin8),
    .D4(n74245_1_pin9), .D1(n74245_1_pin6), .Q2(n74161_1_pin14[8]), .Q3(n74161_1_pin14[9]),
    .Q4(n74161_1_pin14[10]), .Q1(n74161_1_pin14[7]));  // open: CLR, M, N
  _74245 u_74245_2 (
    .pin1(n74245_2_pin1), .pin2(n74245_2_pin2), .pin3(n74245_2_pin3), .pin4(n74245_2_pin4),
    .pin5(n74245_2_pin5), .pin6(n74245_2_pin6), .pin7(n74245_2_pin7), .pin8(n74245_2_pin8),
    .pin9(n74245_2_pin9), .pin19(n74138_2_pin14), .pin18(n74245_1_pin2), .pin17(n74245_1_pin3),
    .pin16(n74245_1_pin4), .pin15(n74245_1_pin5), .pin14(n74245_1_pin6), .pin13(n74245_1_pin7),
    .pin12(n74245_1_pin8), .pin11(n74245_1_pin9));
  // _74181 74181_1: pin names not known; wires that end beside it: n74181_1_p1, n74245_2_pin3, n74245_2_pin2, n74181_1_p4, rom_2_data[0], n74245_2_pin4, rom_2_data[1], n74181_1_p8, rom_2_data[2], n74245_2_pin5, rom_2_data[3], n74181_1_p12, 1'b1, n74181_1_p14, n74181_1_p15, n74181_1_p16, n74181_1_p17, n74181_1_p18
  c74173 c74173_3 (
    .CLK(n74161_1_pin2), .nG1(n74138_1_pin14), .nG2(n74138_1_pin14), .D2(n74245_1_pin3), .D3(n74245_1_pin4),
    .D4(n74245_1_pin5), .D1(n74245_1_pin2), .Q2(n74245_2_pin3), .Q3(n74245_2_pin4), .Q4(n74245_2_pin5),
    .Q1(n74245_2_pin2));  // open: CLR, M, N
  c74173 c74173_4 (
    .CLK(n74161_1_pin2), .nG1(n74138_1_pin14), .nG2(n74138_1_pin14), .D2(n74245_1_pin7), .D3(n74245_1_pin8),
    .D4(n74245_1_pin9), .D1(n74245_1_pin6), .Q2(n74245_2_pin7), .Q3(n74245_2_pin8), .Q4(n74245_2_pin9),
    .Q1(n74245_2_pin6));  // open: CLR, M, N
  // _74181 74181_2: pin names not known; wires that end beside it: n74181_2_p1, n74245_2_pin7, n74245_2_pin6, n74181_2_p4, rom_2_data[3], n74245_2_pin8, rom_2_data[2], n74181_2_p8, rom_2_data[1], n74245_2_pin9, rom_2_data[0], n74181_2_p12, n74181_1_p14, n74181_2_p14, n74181_2_p15, n74181_2_p16, n74181_2_p17
  _74245 u_74245_3 (
    .pin2(n74245_1_pin2), .pin3(n74245_1_pin3), .pin4(n74245_1_pin4), .pin5(n74245_1_pin5),
    .pin6(n74245_1_pin6), .pin7(n74245_1_pin7), .pin8(n74245_1_pin8), .pin9(n74245_1_pin9),
    .pin19(n74138_2_pin12), .pin18(n74181_1_p15), .pin17(n74181_1_p16), .pin16(n74181_1_p17),
    .pin15(n74181_1_p18), .pin14(n74181_2_p14), .pin13(n74181_2_p15), .pin12(n74181_2_p16),
    .pin11(n74181_2_p17));  // open: pin1
  _7402 u_7402_2 (
    .pin1(n7402_2_pin1), .pin2(n74181_1_p15), .pin3(n74181_1_p16), .pin4(n7402_2_pin4), .pin5(n74181_1_p17),
    .pin6(n74181_1_p18), .pin13(n7402_2_pin13), .pin12(n74181_2_p14), .pin11(n74181_2_p15),
    .pin10(n7402_2_pin10), .pin9(n74181_2_p16), .pin8(n74181_2_p17));
  _74245 u_74245_4 (
    .pin1(n74245_4_pin1), .pin2(n74181_1_p1), .pin3(n74181_1_p4), .pin4(n74181_1_p8), .pin5(n74181_1_p12),
    .pin6(n74181_2_p1), .pin7(n74181_2_p4), .pin8(n74181_2_p8), .pin9(n74181_2_p12), .pin19(n74138_2_pin13),
    .pin18(n74245_1_pin2), .pin17(n74245_1_pin3), .pin16(n74245_1_pin4), .pin15(n74245_1_pin5),
    .pin14(n74245_1_pin6), .pin13(n74245_1_pin7), .pin12(n74245_1_pin8), .pin11(n74245_1_pin9));
  _7408 u_7408_1 (
    .pin1(n7402_2_pin4), .pin2(n7402_2_pin1), .pin3(n7408_1_pin3), .pin13(n7402_2_pin10),
    .pin12(n7402_2_pin13), .pin11(n7408_1_pin11));  // open: pin4, pin5, pin6, pin10, pin9, pin8
  _7408 u_7408_2 (
    .pin13(n7408_1_pin3), .pin12(n7408_1_pin11), .pin11(n7408_2_pin11));  // open: pin1, pin2, pin3, pin4, pin5, pin6, pin10, pin9, pin8
  c74173 c74173_5 (
    .CLK(n74161_1_pin2), .nG1(n74138_1_pin13), .nG2(n74138_1_pin13), .D2(n74245_1_pin3), .D3(n74245_1_pin4),
    .D4(n74245_1_pin5), .D1(n74245_1_pin2), .Q2(n74181_1_p4), .Q3(n74181_1_p8), .Q4(n74181_1_p12),
    .Q1(n74181_1_p1));  // open: CLR, M, N
  c74173 c74173_6 (
    .CLK(n74161_1_pin2), .nG1(n7402_1_pin10), .nG2(n7402_1_pin10), .D1(n7408_2_pin11), .Q1(n74161_1_pin14[4]));  // open: CLR, M, N, D2, D3, D4, Q2, Q3, Q4
  DipSwitch #(.number(4)) dipswitch_1 (
    .sw1(dipswitch_1_sw1), .sw2(dipswitch_1_sw2), .sw3(dipswitch_1_sw3), .sw4(dipswitch_1_sw4));
  c74173 c74173_7 (
    .CLK(n74161_1_pin2), .nG1(n74138_1_pin11), .nG2(n74138_1_pin11), .D2(n74157_1_pin7), .D3(n74157_1_pin9),
    .D4(n74157_1_pin12), .D1(n74157_1_pin4), .Q2(c74173_7_q1[1]), .Q3(c74173_7_q1[2]), .Q4(c74173_7_q1[3]),
    .Q1(c74173_7_q1[0]));  // open: CLR, M, N
  _74157 u_74157_1 (
    .pin1(in_1), .pin2(n74245_1_pin2), .pin3(dipswitch_1_sw4), .pin4(n74157_1_pin4), .pin5(n74245_1_pin3),
    .pin6(dipswitch_1_sw3), .pin7(n74157_1_pin7), .pin14(n74245_1_pin5), .pin13(dipswitch_1_sw1),
    .pin12(n74157_1_pin12), .pin11(n74245_1_pin4), .pin10(dipswitch_1_sw2), .pin9(n74157_1_pin9));  // open: pin15
  c74173 c74173_8 (
    .CLK(n74161_1_pin2), .nG1(n74138_1_pin13), .nG2(n74138_1_pin13), .D2(n74245_1_pin7), .D3(n74245_1_pin8),
    .D4(n74245_1_pin9), .D1(n74245_1_pin6), .Q2(n74181_2_p4), .Q3(n74181_2_p8), .Q4(n74181_2_p12),
    .Q1(n74181_2_p1));  // open: CLR, M, N
  _74157 u_74157_2 (
    .pin1(in_2), .pin2(n74245_1_pin2), .pin3(n74157_2_pin3), .pin4(n74157_2_pin4[0]), .pin5(n74245_1_pin3),
    .pin6(n74157_2_pin6), .pin7(n74157_2_pin4[1]), .pin14(n74245_1_pin5), .pin13(n74157_2_pin13),
    .pin12(n74157_2_pin4[3]), .pin11(n74245_1_pin4), .pin10(n74157_2_pin10), .pin9(n74157_2_pin4[2]));  // open: pin15
  DipSwitch dipswitch_2 (
    .sw1(n74157_2_pin3), .sw2(n74157_2_pin6), .sw3(n74157_2_pin10), .sw4(n74157_2_pin13),
    .sw5(dipswitch_2_sw5), .sw6(dipswitch_2_sw6), .sw7(dipswitch_2_sw7), .sw8(dipswitch_2_sw8));
  _74157 u_74157_3 (
    .pin1(in_3), .pin2(n74245_1_pin6), .pin3(dipswitch_2_sw5), .pin4(n74157_2_pin4[4]), .pin5(n74245_1_pin7),
    .pin6(dipswitch_2_sw6), .pin7(n74157_2_pin4[5]), .pin14(n74245_1_pin9), .pin13(dipswitch_2_sw8),
    .pin12(n74157_2_pin4[7]), .pin11(n74245_1_pin8), .pin10(dipswitch_2_sw7), .pin9(n74157_2_pin4[6]));  // open: pin15
  RAM #(.addrWidth(4)) ram_1 (
    .addr(c74173_7_q1), .we(not_1_out), .oe(n74138_1_pin10), .clk(n74161_1_pin2), .din(n74157_2_pin4),
    .dout(ram_1_dout));
  not not_1 (not_1_out, n74138_1_pin10);
  _74245 u_74245_5 (
    .pin2(n74245_1_pin2), .pin3(n74245_1_pin3), .pin4(n74245_1_pin4), .pin5(n74245_1_pin5),
    .pin6(n74245_1_pin6), .pin7(n74245_1_pin7), .pin8(n74245_1_pin8), .pin9(n74245_1_pin9),
    .pin19(n74138_2_pin10), .pin18(ram_1_dout[0]), .pin17(ram_1_dout[1]), .pin16(ram_1_dout[2]),
    .pin15(ram_1_dout[3]), .pin14(ram_1_dout[4]), .pin13(ram_1_dout[5]), .pin12(ram_1_dout[6]),
    .pin11(ram_1_dout[7]));  // open: pin1
  LED led_1 (.in(c74173_9_q1));
  LED led_2 (.in(c74173_9_q2));
  LED led_3 (.in(c74173_9_q3));
  LED led_4 (.in(c74173_9_q4));
  c74173 c74173_9 (
    .CLK(n74161_1_pin2), .nG1(n74138_1_pin12), .nG2(n74138_1_pin12), .D2(n74245_1_pin3), .D3(n74245_1_pin4),
    .D4(n74245_1_pin5), .D1(n74245_1_pin2), .Q2(c74173_9_q2), .Q3(c74173_9_q3), .Q4(c74173_9_q4),
    .Q1(c74173_9_q1));  // open: CLR, M, N
  LED led_5 (.in(c74173_10_q1));
  LED led_6 (.in(c74173_10_q2));
  LED led_7 (.in(c74173_10_q3));
  LED led_8 (.in(c74173_10_q4));
  _74161 u_74161_2 (
    .pin1(n7402_1_pin1), .pin2(n74161_1_pin2), .pin3(n74245_1_pin2), .pin4(n74245_1_pin3),
    .pin5(n74245_1_pin4), .pin6(n74245_1_pin5), .pin7(rom_2_data[5]), .pin14(n74161_2_pin14),
    .pin13(n74161_2_pin13), .pin12(n74161_2_pin12), .pin11(n74161_2_pin11), .pin10(rom_2_data[5]),
    .pin9(n74138_1_pin9));  // open: pin15
  c74173 c74173_10 (
    .CLK(n74161_1_pin2), .nG1(n74138_1_pin12), .nG2(n74138_1_pin12), .D2(n74245_1_pin7), .D3(n74245_1_pin8),
    .D4(n74245_1_pin9), .D1(n74245_1_pin6), .Q2(c74173_10_q2), .Q3(c74173_10_q3), .Q4(c74173_10_q4),
    .Q1(c74173_10_q1));  // open: CLR, M, N
  _74245 u_74245_6 (
    .pin2(n74245_1_pin2), .pin3(n74245_1_pin3), .pin4(n74245_1_pin4), .pin5(n74245_1_pin5),
    .pin6(n74245_1_pin6), .pin7(n74245_1_pin7), .pin8(n74245_1_pin8), .pin9(n74245_1_pin9),
    .pin19(n74138_2_pin9), .pin18(n74161_2_pin14), .pin17(n74161_2_pin13), .pin16(n74161_2_pin12),
    .pin15(n74161_2_pin11), .pin14(n74245_6_pin14), .pin13(n74245_6_pin14), .pin12(n74245_6_pin14),
    .pin11(n74245_6_pin14));  // open: pin1
  _74245 u_74245_7 (
    .pin1(n74245_7_pin1), .pin2(n74245_7_pin2), .pin3(n74245_7_pin3), .pin4(n74245_7_pin4),
    .pin5(n74245_7_pin5), .pin6(n74245_7_pin6), .pin7(n74245_7_pin7), .pin8(n74245_7_pin8),
    .pin9(n74245_7_pin9), .pin19(n74138_2_pin11), .pin18(n74245_1_pin2), .pin17(n74245_1_pin3),
    .pin16(n74245_1_pin4), .pin15(n74245_1_pin5), .pin14(n74245_1_pin6), .pin13(n74245_1_pin7),
    .pin12(n74245_1_pin8), .pin11(n74245_1_pin9));
  DipSwitch dipswitch_3 (
    .sw1(n74245_7_pin9), .sw2(n74245_7_pin8), .sw3(n74245_7_pin7), .sw4(n74245_7_pin6), .sw5(n74245_7_pin5),
    .sw6(n74245_7_pin4), .sw7(n74245_7_pin3), .sw8(n74245_7_pin2));
  // also tied to GND on the sheet: {n7402_1_pin3, n7402_1_pin6, n7402_1_pin8, n74245_1_pin14, n74138_1_pin4, n74138_2_pin4, n74245_6_pin14}
  // also tied to VCC on the sheet: {n74161_1_pin7, n74138_1_pin6, n74138_2_pin6, n74245_2_pin1, n74245_4_pin1, n74245_7_pin1}

  // Notes on the sheet:
  //   contents of rom_1 (hex, n*v repeats v):
  //   34 2f 3c 29 80 155*0 34 2f 11 80 28*0 34 2f 21 80 60*0 34 2f 3c d 80 123*0 34 2f 3c 2a 80 891*0 34
  //   2f 19 80 12*0 34 2f 19 80 492*0 34 2f b 80 124*0 34 2f 80 13*0 34 2f 3e 80
  //   contents of rom_2 (hex, n*v repeats v):
  //   0 0 0 20 158*0 20 31*0 20 64*0 20 127*0 20 894*0 39 15*0 39 495*0 20 126*0 20 16*0 20
endmodule

module c74173 (
  input  D1,
  input  D2,
  input  D3,
  input  D4,
  input  CLK,
  input  nG1,
  input  nG2,
  input  CLR,
  input  M,
  input  N,
  output Q1,
  output Q2,
  output Q3,
  output Q4
);

  wire and_1_out, and_2_out, and_3_out, and_4_out, d_ff_1_q, d_ff_2_q, d_ff_3_q, d_ff_4_q, nor_1_out,
       nor_2_out;

  and and_1 (and_1_out, CLK, nor_1_out);
  and and_2 (and_2_out, CLK, nor_1_out);
  and and_3 (and_3_out, CLK, nor_1_out);
  and and_4 (and_4_out, CLK, nor_1_out);
  nor nor_1 (nor_1_out, nG1, nG2);
  D_Flip_Flop d_ff_1 (.D(D1), .clk(and_1_out), .Q(d_ff_1_q), .reset(CLR));  // open: Qn, preset
  D_Flip_Flop d_ff_2 (.D(D2), .clk(and_2_out), .Q(d_ff_2_q), .reset(CLR));  // open: Qn, preset
  D_Flip_Flop d_ff_3 (.D(D3), .clk(and_3_out), .Q(d_ff_3_q), .reset(CLR));  // open: Qn, preset
  D_Flip_Flop d_ff_4 (.D(D4), .clk(and_4_out), .Q(d_ff_4_q), .reset(CLR));  // open: Qn, preset
  nor nor_2 (nor_2_out, M, N);
  assign Q1 = nor_2_out ? d_ff_1_q : 1'bz;  // Controlled_Buffer controlled_buffer_1
  assign Q2 = nor_2_out ? d_ff_2_q : 1'bz;  // Controlled_Buffer controlled_buffer_2
  assign Q3 = nor_2_out ? d_ff_3_q : 1'bz;  // Controlled_Buffer controlled_buffer_3
  assign Q4 = nor_2_out ? d_ff_4_q : 1'bz;  // Controlled_Buffer controlled_buffer_4
endmodule
