// Logisim project BC.circ as structural Verilog: 12 circuits, main circuit main
module main (
  input  [7:0] in_1,
  input  [3:0] in_2,
  output [3:0] out_3,
  output [7:0] out_4,
  output [3:0] out_5,
  output [1:0] out_6
);

  wire clu_1_x1, clu_1_x2, clu_1_x3, clu_1_x4, clu_1_x5, clu_1_x6, clu_1_x7, clu_1_x8, clu_1_x12, clu_1_x13,
       decoder_1_out1, decoder_1_out2, decoder_1_out3, decoder_1_out4, decoder_1_out5, decoder_1_out7,
       not_1_out, not_2_out, not_3_out, or_1_out, or_2_out;
  wire [1:0] clu_1_x10, clu_1_x11;
  wire [3:0] adder_1_out, IR_q_2, MAR_q, MBR_q, MBR_q_2, multiplexer_1_out, multiplexer_2_out, register_2_q,
       t_1_q;
  wire [7:0] alu_1_q, multiplexer_3_out, multiplexer_4_out, multiplexer_5_out;
  wire [7:4] IR_q;

  Multiplexer #(.width(4)) multiplexer_1 (.in0(out_5), .in1(adder_1_out), .out(multiplexer_1_out), .sel(clu_1_x3));
  or or_1 (or_1_out, clu_1_x3, clu_1_x13);
  not not_1 (not_1_out, or_1_out);
  Register #(.width(4)) register_1 (.D(multiplexer_1_out), .en(or_2_out), .clk(not_2_out), .Q(out_3));  // open: clr
  or or_2 (or_2_out, clu_1_x3, clu_1_x13);
  not not_2 (not_2_out, not_1_out);
  Register IR (.D({MBR_q_2, MBR_q}), .en(clu_1_x1), .clk(clu_1_x1), .Q({IR_q, IR_q_2}));  // open: clr
  not not_3 (not_3_out, clu_1_x6);
  Adder #(.width(4)) adder_1 (.a(out_3), .b(4'b0001), .out(adder_1_out));  // open: cin, cout
  Decoder #(.select(4)) decoder_1 (
    .out1(decoder_1_out1), .out2(decoder_1_out2), .out3(decoder_1_out3), .out4(decoder_1_out4),
    .out5(decoder_1_out5), .out7(decoder_1_out7), .sel(IR_q));  // open: out0, out6, out8, out9, out10, out11, out12, out13, out14, out15, en
  T t_1 (.INC(not_3_out), .CLEAR(clu_1_x6), .Q(t_1_q));
  Multiplexer #(.select(2), .width(4)) multiplexer_2 (
    .in0(out_3), .in1(IR_q_2), .in2(MBR_q), .out(multiplexer_2_out), .sel(clu_1_x10));  // open: in3
  Register #(.width(4)) MAR (.D(multiplexer_2_out), .en(clu_1_x4), .clk(clu_1_x4), .Q(MAR_q));  // open: clr
  Register MBR (.D(multiplexer_3_out), .en(clu_1_x2), .clk(clu_1_x2), .Q({MBR_q_2, MBR_q}));  // open: clr
  Multiplexer #(.width(8)) multiplexer_3 (
    .in0(out_4), .in1({register_2_q, out_5}), .out(multiplexer_3_out), .sel(clu_1_x7));
  CLU clu_1 (
    .q1(decoder_1_out1), .q2(decoder_1_out2), .q3(decoder_1_out3), .q4(decoder_1_out4), .q5(decoder_1_out5),
    .q7(decoder_1_out7), .t(t_1_q), .x1(clu_1_x1), .x2(clu_1_x2), .x3(clu_1_x3), .x4(clu_1_x4),
    .x5(clu_1_x5), .x6(clu_1_x6), .x7(clu_1_x7), .x8(clu_1_x8), .x9(out_6), .x10(clu_1_x10), .x11(clu_1_x11),
    .x12(clu_1_x12), .x13(clu_1_x13));
  Multiplexer #(.select(2), .width(8)) multiplexer_4 (
    .in0({MBR_q_2, MBR_q}), .in1({4'b0000, IR_q_2}), .in2({4'b0000, out_3}), .in3(alu_1_q),
    .out(multiplexer_4_out), .sel(clu_1_x11));
  Multiplexer #(.width(8)) multiplexer_5 (
    .in0({MBR_q_2, MBR_q}), .in1({register_2_q, out_5}), .out(multiplexer_5_out), .sel(clu_1_x8));
  Memory_Unit memory_unit_1 (.D({MBR_q_2, MBR_q}), .R(clu_1_x5), .S(MAR_q), .out_4(out_4));
  Register register_2 (.D(multiplexer_4_out), .en(clu_1_x12), .clk(clu_1_x12), .Q({register_2_q, out_5}));  // open: clr
  ALU alu_1 (.D(multiplexer_5_out), .LOAF(out_6), .Q(alu_1_q));
endmodule

module Memory_Unit (
  input  [7:0] D,
  input  R,
  input  [3:0] S,
  output [7:0] out_4
);

  wire decoder_1_out0, decoder_1_out1, decoder_1_out2, decoder_1_out3;
  wire [7:0] register_1_q, register_2_q, register_3_q, register_4_q;

  Decoder #(.select(4)) decoder_1 (
    .out0(decoder_1_out0), .out1(decoder_1_out1), .out2(decoder_1_out2), .out3(decoder_1_out3), .sel(S));  // open: out4, out5, out6, out7, out8, out9, out10, out11, out12, out13, out14, out15, en
  Register register_1 (.D(D), .en(decoder_1_out0), .clk(R), .Q(register_1_q));  // open: clr
  Register register_2 (.D(D), .en(decoder_1_out1), .clk(R), .Q(register_2_q));  // open: clr
  Register register_3 (.D(D), .en(decoder_1_out2), .clk(R), .Q(register_3_q));  // open: clr
  Register register_4 (.D(D), .en(decoder_1_out3), .clk(R), .Q(register_4_q));  // open: clr
  Multiplexer #(.select(4), .width(8)) multiplexer_1 (
    .in0(register_1_q), .in1(register_2_q), .in2(register_3_q), .in3(register_4_q), .out(out_4), .sel(S));  // open: in4, in5, in6, in7, in8, in9, in10, in11, in12, in13, in14, in15
endmodule

module LDA (
  input  q1,
  input  t3,
  input  t4,
  input  t5,
  input  t6,
  output x4,
  output x2,
  output x12,
  output x6
);

  and and_1 (x4, t3, q1);
  and and_2 (x2, t4, q1);
  and and_3 (x12, t5, q1);
  and and_4 (x6, t6, q1);
endmodule

module LDI (
  input  q2,
  input  t3,
  input  t4,
  input  t5,
  input  t6,
  input  t7,
  input  t8,
  output x4_1,
  output x2_1,
  output x10_10,
  output x4_2,
  output x2_2,
  output x12,
  output x6
);

  and and_1 (x4_1, t3, q2);
  and and_2 (x2_1, t4, q2);
  and and_3 (x4_2, t5, q2);
  and and_4 (x2_2, t6, q2);
  and and_5 (x12, t7, q2);
  and and_6 (x6, t8, q2);

  assign x10_10 = x4_2;
endmodule

module STA (
  input  q3,
  input  t3,
  input  t4,
  input  t5,
  input  t6,
  output x7,
  output x3,
  output x4,
  output x5,
  output x6
);

  and and_1 (x3, t3, q3);
  and and_2 (x4, t4, q3);
  and and_3 (x5, t5, q3);
  and and_4 (x6, t6, q3);

  assign x7 = x3;
endmodule

module STI (
  input  q4,
  input  t3,
  input  t4,
  input  t5,
  input  t6,
  input  t7,
  input  t8,
  output x4_1,
  output x2_1,
  output x10_10,
  output x4_2,
  output x7,
  output x2_2,
  output x5,
  output x6
);

  and and_1 (x4_1, t3, q4);
  and and_2 (x2_1, t4, q4);
  and and_3 (x4_2, t5, q4);
  and and_4 (x2_2, t6, q4);
  and and_5 (x5, t7, q4);
  buf and_6 (x6, t8);  // AND_Gate

  assign x7 = x2_2;
  assign x10_10 = x4_2;
endmodule

module ADD (
  input  q5,
  input  t3,
  input  t4,
  input  t5,
  input  t6,
  input  t7,
  input  t8,
  output x4_1,
  output x2,
  output x9_01,
  output x8,
  output x9_10,
  output x11_11,
  output x12,
  output x6
);

  and and_1 (x4_1, t3, q5);
  and and_2 (x2, t4, q5);
  and and_3 (x9_01, t5, q5);
  and and_4 (x8, t6, q5);
  and and_5 (x11_11, t7, q5);
  and and_6 (x6, t8, q5);

  assign x9_10 = x8;
  assign x12 = x11_11;
endmodule

module JMP (
  input  q7,
  input  t3,
  input  t4,
  input  t5,
  input  t6,
  input  t7,
  input  t8,
  input  t9,
  output x11_10,
  output x12_1,
  output x8_1,
  output x9_01,
  output x11_01,
  output x12_2,
  output x8_2,
  output x9_10,
  output x11_11,
  output x12_3,
  output x3,
  output x6
);

  and and_1 (x11_10, t3, q7);
  and and_2 (x8_1, t4, q7);
  and and_3 (x11_01, t5, q7);
  and and_4 (x8_2, t6, q7);
  and and_5 (x11_11, t7, q7);
  and and_6 (x3, t8, q7);
  and and_7 (x6, t9, q7);

  assign x9_01 = x8_1;
  assign x9_10 = x8_2;
  assign x12_1 = x11_10;
  assign x12_2 = x11_01;
  assign x12_3 = x11_11;
endmodule

module CLU (
  input  q1,
  input  q2,
  input  q3,
  input  q4,
  input  q5,
  input  q7,
  input  [3:0] t,
  output x1,
  output x2,
  output x3,
  output x4,
  output x5,
  output x6,
  output x7,
  output x8,
  output [1:0] x9,
  output [1:0] x10,
  output [1:0] x11,
  output x12,
  output x13
);

  wire add_1_x2, add_1_x4_1, add_1_x6, add_1_x8, add_1_x9_01, add_1_x9_10, add_1_x11_11, add_1_x12,
       decoder_1_out0, decoder_1_out3, decoder_1_out4, decoder_1_out5, decoder_1_out6, decoder_1_out7,
       decoder_1_out8, decoder_1_out9, decoder_1_out10, decoder_1_out11, jmp_1_x6, jmp_1_x8_1, jmp_1_x8_2,
       jmp_1_x9_01, jmp_1_x9_10, jmp_1_x11_01, jmp_1_x11_10, jmp_1_x11_11, jmp_1_x12_1, jmp_1_x12_2,
       jmp_1_x12_3, lda_1_x2, lda_1_x4, lda_1_x6, lda_1_x12, ldi_1_x2_1, ldi_1_x2_2, ldi_1_x4_1, ldi_1_x4_2,
       ldi_1_x6, ldi_1_x10_10, ldi_1_x12, or_1_out, or_2_out, or_3_out, or_4_out, or_9_out, or_10_out,
       or_11_out, or_12_out, or_14_out, or_15_out, sta_1_x3, sta_1_x4, sta_1_x5, sta_1_x6, sta_1_x7,
       sti_1_x2_1, sti_1_x2_2, sti_1_x4_1, sti_1_x4_2, sti_1_x5, sti_1_x6, sti_1_x7, sti_1_x10_10;

  Decoder #(.select(4)) decoder_1 (
    .out0(decoder_1_out0), .out1(x13), .out2(x1), .out3(decoder_1_out3), .out4(decoder_1_out4),
    .out5(decoder_1_out5), .out6(decoder_1_out6), .out7(decoder_1_out7), .out8(decoder_1_out8),
    .out9(decoder_1_out9), .out10(decoder_1_out10), .out11(decoder_1_out11), .sel(t));  // open: out12, out13, out14, out15, en
  LDA lda_1 (
    .q1(q1), .t3(decoder_1_out3), .t4(decoder_1_out4), .t5(decoder_1_out5), .t6(decoder_1_out6),
    .x4(lda_1_x4), .x2(lda_1_x2), .x12(lda_1_x12), .x6(lda_1_x6));
  LDI ldi_1 (
    .q2(q2), .t3(decoder_1_out3), .t4(decoder_1_out4), .t5(decoder_1_out5), .t6(decoder_1_out6),
    .t7(decoder_1_out7), .t8(decoder_1_out8), .x4_1(ldi_1_x4_1), .x2_1(ldi_1_x2_1), .x10_10(ldi_1_x10_10),
    .x4_2(ldi_1_x4_2), .x2_2(ldi_1_x2_2), .x12(ldi_1_x12), .x6(ldi_1_x6));
  STA sta_1 (
    .q3(q3), .t3(decoder_1_out3), .t4(decoder_1_out4), .t5(decoder_1_out5), .t6(decoder_1_out6),
    .x7(sta_1_x7), .x3(sta_1_x3), .x4(sta_1_x4), .x5(sta_1_x5), .x6(sta_1_x6));
  STI sti_1 (
    .q4(q4), .t3(decoder_1_out3), .t4(decoder_1_out4), .t5(decoder_1_out5), .t6(decoder_1_out6),
    .t7(decoder_1_out7), .t8(decoder_1_out8), .x4_1(sti_1_x4_1), .x2_1(sti_1_x2_1), .x10_10(sti_1_x10_10),
    .x4_2(sti_1_x4_2), .x7(sti_1_x7), .x2_2(sti_1_x2_2), .x5(sti_1_x5), .x6(sti_1_x6));
  ADD add_1 (
    .q5(q5), .t3(decoder_1_out3), .t4(decoder_1_out4), .t5(decoder_1_out5), .t6(decoder_1_out6),
    .t7(decoder_1_out7), .t8(decoder_1_out8), .x4_1(add_1_x4_1), .x2(add_1_x2), .x9_01(add_1_x9_01),
    .x8(add_1_x8), .x9_10(add_1_x9_10), .x11_11(add_1_x11_11), .x12(add_1_x12), .x6(add_1_x6));
  JMP jmp_1 (
    .q7(q7), .t3(decoder_1_out3), .t4(decoder_1_out4), .t5(decoder_1_out5), .t6(decoder_1_out6),
    .t7(decoder_1_out7), .t8(decoder_1_out8), .t9(decoder_1_out9), .x11_10(jmp_1_x11_10),
    .x12_1(jmp_1_x12_1), .x8_1(jmp_1_x8_1), .x9_01(jmp_1_x9_01), .x11_01(jmp_1_x11_01), .x12_2(jmp_1_x12_2),
    .x8_2(jmp_1_x8_2), .x9_10(jmp_1_x9_10), .x11_11(jmp_1_x11_11), .x12_3(jmp_1_x12_3), .x3(x3), .x6(jmp_1_x6));
  or or_1 (or_1_out, x13, add_1_x2);
  or or_2 (or_2_out, jmp_1_x8_1, jmp_1_x8_2);
  or or_3 (or_3_out, sti_1_x2_1, sti_1_x2_2, or_1_out);
  or or_4 (or_4_out, add_1_x4_1, sti_1_x4_2);
  or or_5 (x5, sti_1_x5, sta_1_x5);
  or or_6 (x9[0], jmp_1_x9_01, add_1_x9_01);
  or or_7 (x9[1], add_1_x9_10, jmp_1_x9_10);
  or or_8 (x10[1], sti_1_x10_10, ldi_1_x10_10);
  or or_9 (or_9_out, ldi_1_x2_2, sta_1_x3, or_3_out);
  or or_10 (or_10_out, ldi_1_x4_2, sta_1_x4, sti_1_x4_1, or_4_out);
  or or_11 (or_11_out, sta_1_x6, sti_1_x6, jmp_1_x6);
  or or_12 (or_12_out, decoder_1_out0, x10[1]);
  or or_13 (x11[1], add_1_x11_11, jmp_1_x11_11, jmp_1_x11_10);
  or or_14 (or_14_out, add_1_x12, jmp_1_x12_1, or_15_out);
  or or_15 (or_15_out, jmp_1_x12_2, jmp_1_x12_3);
  or or_16 (x2, ldi_1_x2_1, lda_1_x2, or_9_out);
  or or_17 (x4, decoder_1_out0, lda_1_x4, ldi_1_x4_1, or_10_out);
  or or_18 (x6, lda_1_x6, ldi_1_x6, or_11_out);
  or or_19 (x7, sta_1_x7, sti_1_x7);
  or or_20 (x8, add_1_x8, or_2_out, add_1_x6);
  not not_1 (x10[0], or_12_out);
  or or_21 (x11[0], jmp_1_x11_01, jmp_1_x11_11, add_1_x11_11);
  or or_22 (x12, lda_1_x12, ldi_1_x12, or_14_out);
endmodule

module T (
  input  INC,
  input  CLEAR,
  output [3:0] Q
);

  wire clock_1_out;
  wire [3:0] adder_1_out;

  Clock clock_1 (.out(clock_1_out));
  Register #(.width(4)) register_1 (.D(adder_1_out), .en(INC), .clk(clock_1_out), .Q(Q), .clr(CLEAR));
  Adder #(.width(4)) adder_1 (.a(Q), .b(4'b0001), .out(adder_1_out));  // open: cin, cout
endmodule

module PC (
  input  [3:0] D,
  input  INC,
  input  LOAD,
  output [3:0] out_4
);

  wire not_1_out, not_2_out, or_1_out, or_2_out;
  wire [3:0] adder_1_out, multiplexer_1_out;

  Multiplexer #(.width(4)) multiplexer_1 (.in0(D), .in1(adder_1_out), .out(multiplexer_1_out), .sel(INC));
  or or_1 (or_1_out, INC, LOAD);
  or or_2 (or_2_out, INC, LOAD);
  not not_1 (not_1_out, or_1_out);
  not not_2 (not_2_out, not_1_out);
  Register #(.width(4)) register_1 (.D(multiplexer_1_out), .en(or_2_out), .clk(not_2_out), .Q(out_4));  // open: clr
  Adder #(.width(4)) adder_1 (.a(out_4), .b(4'b0001), .out(adder_1_out));  // open: cin, cout
endmodule

module ALU (
  input  [7:0] D,
  input  [1:0] LOAF,
  output [7:0] Q
);

  wire not_1_out, not_2_out, or_1_out;
  wire [7:0] adder_1_out, multiplexer_1_out;

  Adder adder_1 (.a(Q), .b(D), .out(adder_1_out));  // open: cin, cout
  Multiplexer #(.select(2), .width(8)) multiplexer_1 (
    .in1(D), .in2(adder_1_out), .out(multiplexer_1_out), .sel(LOAF));  // open: in0, in3
  or or_1 (or_1_out, LOAF[0], LOAF[1]);
  Register register_1 (.D(multiplexer_1_out), .en(not_1_out), .clk(not_1_out), .Q(Q));  // open: clr
  not not_1 (not_1_out, not_2_out);
  not not_2 (not_2_out, or_1_out);
endmodule
