// Logisim project SC.circ as structural Verilog: 38 circuits, main circuit main
module main (
  input  [7:0] in_1,
  input  [3:0] in_2,
  input  in_3,
  input  in_4,
  output [7:0] out_5,
  output [3:0] out_6,
  output [7:0] out_7,
  output [7:0] out_8,
  output [3:0] out_9,
  output [3:0] out_10
);

  wire clu_1_x1, clu_1_x2, clu_1_x3, clu_1_x4, clu_1_x5, clu_1_x6, clu_1_x7, clu_1_x8, clu_1_x12, clu_1_x13,
       dec_4x16_1_b1, dec_4x16_1_b2, dec_4x16_1_b3, dec_4x16_1_b4, dec_4x16_1_b5, dec_4x16_1_b7, not_1_out,
       not_2_out, or_1_out, or_2_out;
  wire [1:0] clu_1_x9, clu_1_x10, clu_1_x11;
  wire [3:0] drop_4_1_q, drop_4_2_q, mplxr_4x1_4_bit_1_q, pc_1_q, t_1_out_3;
  wire [7:0] add_4_1_q, add_4_2_q, alu_1_out_3, mplxr_2x1_8_bit_1_q, mplxr_2x1_8_bit_2_q, mplxr_4x1_8_bit_1_q;

  Drop_4 drop_4_1 (.D(out_8), .Q(drop_4_1_q));
  PC pc_1 (.D(drop_4_1_q), .LOAD(clu_1_x3), .INC(clu_1_x13), .Q(pc_1_q));
  Register_8_Bit_Dual register_8_bit_dual_1 (.D(out_7), .LOAD(clu_1_x1), .Q1(out_10), .Q2(out_9));
  Drop_4 drop_4_2 (.D(out_7), .Q(drop_4_2_q));
  Mplxr_4x1_4_Bit mplxr_4x1_4_bit_1 (
    .D0(pc_1_q), .D1(out_10), .D2(drop_4_2_q), .S(clu_1_x10), .Q(mplxr_4x1_4_bit_1_q));  // open: D3
  Dec_4x16 dec_4x16_1 (
    .D(out_9), .B1(dec_4x16_1_b1), .B2(dec_4x16_1_b2), .B3(dec_4x16_1_b3), .B4(dec_4x16_1_b4),
    .B5(dec_4x16_1_b5), .B7(dec_4x16_1_b7));  // open: B0, B6, B8, B9, B10, B11, B12, B13, B14, B15
  Add_4 add_4_1 (.D(pc_1_q), .Q(add_4_1_q));
  or or_1 (or_1_out, clu_1_x5, in_3);
  not not_1 (not_1_out, or_1_out);
  Register_4_Bit MAR (.D(mplxr_4x1_4_bit_1_q), .LOAD(clu_1_x4), .Q(out_6));
  CLU clu_1 (
    .q1(dec_4x16_1_b1), .q2(dec_4x16_1_b2), .q3(dec_4x16_1_b3), .q4(dec_4x16_1_b4), .q5(dec_4x16_1_b5),
    .q7(dec_4x16_1_b7), .t(t_1_out_3), .x1(clu_1_x1), .x2(clu_1_x2), .x3(clu_1_x3), .x4(clu_1_x4),
    .x5(clu_1_x5), .x6(clu_1_x6), .x7(clu_1_x7), .x8(clu_1_x8), .x9(clu_1_x9), .x10(clu_1_x10),
    .x11(clu_1_x11), .x12(clu_1_x12), .x13(clu_1_x13));
  Mplxr_2x1_8_Bit mplxr_2x1_8_bit_1 (.D0(out_5), .D1(out_8), .S(clu_1_x7), .Q(mplxr_2x1_8_bit_1_q));
  or or_2 (or_2_out, in_4, clu_1_x6);
  not not_2 (not_2_out, or_2_out);
  Register_8_Bit MBR (.D(mplxr_2x1_8_bit_1_q), .LOAD(clu_1_x2), .Q(out_7));
  Add_4 add_4_2 (.D(out_10), .Q(add_4_2_q));
  T t_1 (.INC(not_2_out), .CLR(or_2_out), .out_3(t_1_out_3));
  Memory_Unit memory_unit_1 (.R_W(not_1_out), .D(out_7), .S(out_6), .Q(out_5));
  Mplxr_2x1_8_Bit mplxr_2x1_8_bit_2 (.D0(out_7), .D1(out_8), .S(clu_1_x8), .Q(mplxr_2x1_8_bit_2_q));
  Mplxr_4x1_8_Bit mplxr_4x1_8_bit_1 (
    .D0(out_7), .D1(add_4_2_q), .D2(add_4_1_q), .D3(alu_1_out_3), .S(clu_1_x11), .Q(mplxr_4x1_8_bit_1_q));
  Register_8_Bit AC (.D(mplxr_4x1_8_bit_1_q), .LOAD(clu_1_x12), .Q(out_8));
  ALU alu_1 (.D(mplxr_2x1_8_bit_2_q), .LOAF(clu_1_x9), .out_3(alu_1_out_3));
endmodule

module RS_Flip_Flop (
  input  R,
  input  S,
  output Q
);

  wire nand_2_out;

  nand nand_1 (Q, R, nand_2_out);
  nand nand_2 (nand_2_out, Q, S);
endmodule

module Memory_Cell (
  input  R_W,
  input  D,
  input  S,
  output Q
);

  wire nand_1_out, nand_2_out, not_1_out, not_2_out, rs_flip_flop_1_q;

  not not_1 (not_1_out, R_W);
  not not_2 (not_2_out, D);
  nand nand_1 (nand_1_out, not_1_out, D, S);
  nand nand_2 (nand_2_out, not_1_out, not_2_out, S);
  RS_Flip_Flop rs_flip_flop_1 (.R(nand_1_out), .S(nand_2_out), .Q(rs_flip_flop_1_q));
  and and_1 (Q, R_W, rs_flip_flop_1_q, S);
endmodule

module Register_8_Bit (
  input  [7:0] D,
  input  LOAD,
  output [7:0] Q
);

  Register_4_Bit register_4_bit_1 (.D(D[3:0]), .LOAD(LOAD), .Q(Q[3:0]));
  Register_4_Bit register_4_bit_2 (.D(D[7:4]), .LOAD(LOAD), .Q(Q[7:4]));
endmodule

module Register_1_Bit (
  input  D,
  input  LOAD,
  output Q
);

  wire nand_1_out, nand_2_out, not_1_out;

  not not_1 (not_1_out, D);
  nand nand_1 (nand_1_out, LOAD, D);
  nand nand_2 (nand_2_out, LOAD, not_1_out);
  RS_Flip_Flop rs_flip_flop_1 (.R(nand_1_out), .S(nand_2_out), .Q(Q));
endmodule

module Register_4_Bit (
  input  [3:0] D,
  input  LOAD,
  output [3:0] Q
);

  Register_1_Bit register_1_bit_1 (.D(D[0]), .LOAD(LOAD), .Q(Q[0]));
  Register_1_Bit register_1_bit_2 (.D(D[1]), .LOAD(LOAD), .Q(Q[1]));
  Register_1_Bit register_1_bit_3 (.D(D[2]), .LOAD(LOAD), .Q(Q[2]));
  Register_1_Bit register_1_bit_4 (.D(D[3]), .LOAD(LOAD), .Q(Q[3]));
endmodule

module Register_8_Bit_Dual (
  input  [7:0] D,
  input  LOAD,
  output [3:0] Q1,
  output [3:0] Q2
);

  Register_8_Bit register_8_bit_1 (.D(D), .LOAD(LOAD), .Q({Q2, Q1}));
endmodule

module Mplxr_4x1 (
  input  D0,
  input  D1,
  input  D2,
  input  D3,
  input  [1:0] S,
  output Q
);

  wire and_1_out, and_2_out, and_3_out, and_4_out, not_1_out, not_2_out;

  not not_1 (not_1_out, S[1]);
  not not_2 (not_2_out, S[0]);
  and and_1 (and_1_out, D0, not_1_out, not_2_out);
  and and_2 (and_2_out, D1, not_1_out, S[0]);
  and and_3 (and_3_out, D2, S[1], not_2_out);
  and and_4 (and_4_out, D3, S[1], S[0]);
  or or_1 (Q, and_1_out, and_2_out, and_3_out, and_4_out);
endmodule

module Mplxr_4x1_4_Bit (
  input  [3:0] D0,
  input  [3:0] D1,
  input  [3:0] D2,
  input  [3:0] D3,
  input  [1:0] S,
  output [3:0] Q
);

  Mplxr_4x1 mplxr_4x1_1 (.D0(D0[0]), .D1(D1[0]), .D2(D2[0]), .D3(D3[0]), .S(S), .Q(Q[0]));
  Mplxr_4x1 mplxr_4x1_2 (.D0(D0[1]), .D1(D1[1]), .D2(D2[1]), .D3(D3[1]), .S(S), .Q(Q[1]));
  Mplxr_4x1 mplxr_4x1_3 (.D0(D0[2]), .D1(D1[2]), .D2(D2[2]), .D3(D3[2]), .S(S), .Q(Q[2]));
  Mplxr_4x1 mplxr_4x1_4 (.D0(D0[3]), .D1(D1[3]), .D2(D2[3]), .D3(D3[3]), .S(S), .Q(Q[3]));
endmodule

module Mplxr_4x1_8_Bit (
  input  [7:0] D0,
  input  [7:0] D1,
  input  [7:0] D2,
  input  [7:0] D3,
  input  [1:0] S,
  output [7:0] Q
);

  Mplxr_4x1_4_Bit mplxr_4x1_4_bit_1 (.D0(D0[3:0]), .D1(D1[3:0]), .D2(D2[3:0]), .D3(D3[3:0]), .S(S), .Q(Q[3:0]));
  Mplxr_4x1_4_Bit mplxr_4x1_4_bit_2 (.D0(D0[7:4]), .D1(D1[7:4]), .D2(D2[7:4]), .D3(D3[7:4]), .S(S), .Q(Q[7:4]));
endmodule

module Mplxr_2x1 (
  input  D0,
  input  D1,
  input  S,
  output Q
);

  wire and_1_out, and_2_out, not_1_out;

  and and_1 (and_1_out, D0, not_1_out);
  not not_1 (not_1_out, S);
  and and_2 (and_2_out, D1, S);
  or or_1 (Q, and_1_out, and_2_out);
endmodule

module Mplxr_2x1_2_Bit (
  input  [1:0] D0,
  input  [1:0] D1,
  input  S,
  output [1:0] Q
);

  Mplxr_2x1 mplxr_2x1_1 (.D0(D0[0]), .D1(D1[0]), .S(S), .Q(Q[0]));
  Mplxr_2x1 mplxr_2x1_2 (.D0(D0[1]), .D1(D1[1]), .S(S), .Q(Q[1]));
endmodule

module Mplxr_2x1_4_Bit (
  input  [3:0] D0,
  input  [3:0] D1,
  input  S,
  output [3:0] out_4
);

  Mplxr_2x1_2_Bit mplxr_2x1_2_bit_1 (.D0(D0[1:0]), .D1(D1[1:0]), .S(S), .Q(out_4[1:0]));
  Mplxr_2x1_2_Bit mplxr_2x1_2_bit_2 (.D0(D0[3:2]), .D1(D1[3:2]), .S(S), .Q(out_4[3:2]));
endmodule

module Mplxr_2x1_8_Bit (
  input  [7:0] D0,
  input  [7:0] D1,
  input  S,
  output [7:0] Q
);

  Mplxr_2x1_4_Bit mplxr_2x1_4_bit_1 (.D0(D0[3:0]), .D1(D1[3:0]), .S(S), .out_4(Q[3:0]));
  Mplxr_2x1_4_Bit mplxr_2x1_4_bit_2 (.D0(D0[7:4]), .D1(D1[7:4]), .S(S), .out_4(Q[7:4]));
endmodule

module Dec_4x16 (
  input  [3:0] D,
  output B0,
  output B1,
  output B2,
  output B3,
  output B4,
  output B5,
  output B6,
  output B7,
  output B8,
  output B9,
  output B10,
  output B11,
  output B12,
  output B13,
  output B14,
  output B15
);

  wire not_1_out, not_2_out, not_3_out, not_4_out;

  not not_1 (not_1_out, D[0]);
  not not_2 (not_2_out, D[1]);
  not not_3 (not_3_out, D[2]);
  not not_4 (not_4_out, D[3]);
  and and_1 (B0, not_1_out, not_2_out, not_3_out, not_4_out);
  and and_2 (B1, D[0], not_2_out, not_3_out, not_4_out);
  and and_3 (B2, not_1_out, D[1], not_3_out, not_4_out);
  and and_4 (B3, D[0], D[1], not_3_out, not_4_out);
  and and_5 (B4, not_1_out, not_2_out, D[2], not_4_out);
  and and_6 (B5, D[0], not_2_out, D[2], not_4_out);
  and and_7 (B6, not_1_out, D[1], D[2], not_4_out);
  and and_8 (B7, D[0], D[1], D[2], not_4_out);
  and and_9 (B8, not_1_out, not_2_out, not_3_out, D[3]);
  and and_10 (B9, D[0], not_2_out, not_3_out, D[3]);
  and and_11 (B10, not_1_out, D[1], not_3_out, D[3]);
  and and_12 (B11, D[0], D[1], not_3_out, D[3]);
  and and_13 (B12, not_1_out, not_2_out, D[2], D[3]);
  and and_14 (B13, D[0], not_2_out, D[2], D[3]);
  and and_15 (B14, not_1_out, D[1], D[2], D[3]);
  and and_16 (B15, D[0], D[1], D[2], D[3]);
endmodule

module Add (
  input  A,
  input  B,
  input  C_IN,
  output SUM,
  output C_OUT
);

  wire and_1_out, and_2_out, xor_1_out;

  xor xor_1 (xor_1_out, A, B);
  and and_1 (and_1_out, A, B);
  and and_2 (and_2_out, xor_1_out, C_IN);
  xor xor_2 (SUM, xor_1_out, C_IN);
  or or_1 (C_OUT, and_2_out, and_1_out);
endmodule

module Add_2_Bit (
  input  [1:0] A,
  input  [1:0] B,
  input  C_IN,
  output [1:0] SUM,
  output C_OUT
);

  wire add_1_c_out;

  Add add_1 (.A(A[0]), .B(B[0]), .C_IN(C_IN), .SUM(SUM[0]), .C_OUT(add_1_c_out));
  Add add_2 (.A(A[1]), .B(B[1]), .C_IN(add_1_c_out), .SUM(SUM[1]), .C_OUT(C_OUT));
endmodule

module Add_4_Bit (
  input  [3:0] A,
  input  [3:0] B,
  input  C_IN,
  output [3:0] SUM,
  output C_OUT
);

  wire add_2_bit_1_c_out;

  Add_2_Bit add_2_bit_1 (.A(A[1:0]), .B(B[1:0]), .C_IN(C_IN), .SUM(SUM[1:0]), .C_OUT(add_2_bit_1_c_out));
  Add_2_Bit add_2_bit_2 (.A(A[3:2]), .B(B[3:2]), .C_IN(add_2_bit_1_c_out), .SUM(SUM[3:2]), .C_OUT(C_OUT));
endmodule

module Add_8_Bit (
  input  [7:0] A,
  input  [7:0] B,
  input  C_IN,
  output [7:0] SUM,
  output C_OUT
);

  wire add_4_bit_1_c_out;

  Add_4_Bit add_4_bit_1 (.A(A[3:0]), .B(B[3:0]), .C_IN(C_IN), .SUM(SUM[3:0]), .C_OUT(add_4_bit_1_c_out));
  Add_4_Bit add_4_bit_2 (.A(A[7:4]), .B(B[7:4]), .C_IN(add_4_bit_1_c_out), .SUM(SUM[7:4]), .C_OUT(C_OUT));
endmodule

module T (
  input  INC,
  input  CLR,
  output [3:0] out_3
);

  wire and_1_out, clock_1_out, not_1_out, not_2_out, not_3_out;
  wire [3:0] add_4_bit_1_sum;

  Clock #(.highDuration(3), .lowDuration(3)) clock_1 (.out(clock_1_out));
  not not_1 (not_1_out, clock_1_out);
  not not_2 (not_2_out, not_1_out);
  not not_3 (not_3_out, not_2_out);
  and and_1 (and_1_out, clock_1_out, INC, not_3_out);
  Register_4_Bit_Clear register_4_bit_clear_1 (.D(add_4_bit_1_sum), .LOAD(and_1_out), .CLR(CLR), .Q(out_3));
  Add_4_Bit add_4_bit_1 (.A(out_3), .B(4'b0001), .SUM(add_4_bit_1_sum));  // open: C_IN, C_OUT
endmodule

module Register_1_Bit_Clear (
  input  D,
  input  LOAD,
  input  CLR,
  output Q
);

  wire and_1_out, nand_1_out, nand_2_out, not_1_out, not_2_out, or_1_out, or_2_out;

  not not_1 (not_1_out, CLR);
  not not_2 (not_2_out, D);
  and and_1 (and_1_out, not_1_out, D);
  or or_1 (or_1_out, CLR, LOAD);
  or or_2 (or_2_out, not_2_out, CLR);
  nand nand_1 (nand_1_out, and_1_out, or_1_out);
  nand nand_2 (nand_2_out, or_1_out, or_2_out);
  RS_Flip_Flop rs_flip_flop_1 (.R(nand_1_out), .S(nand_2_out), .Q(Q));
endmodule

module Register_4_Bit_Clear (
  input  [3:0] D,
  input  LOAD,
  input  CLR,
  output [3:0] Q
);

  Register_1_Bit_Clear register_1_bit_clear_1 (.D(D[0]), .LOAD(LOAD), .CLR(CLR), .Q(Q[0]));
  Register_1_Bit_Clear register_1_bit_clear_2 (.D(D[1]), .LOAD(LOAD), .CLR(CLR), .Q(Q[1]));
  Register_1_Bit_Clear register_1_bit_clear_3 (.D(D[2]), .LOAD(LOAD), .CLR(CLR), .Q(Q[2]));
  Register_1_Bit_Clear register_1_bit_clear_4 (.D(D[3]), .LOAD(LOAD), .CLR(CLR), .Q(Q[3]));
endmodule

module Memory_Unit (
  input  R_W,
  input  [7:0] D,
  input  [3:0] S,
  output [7:0] Q
);

  wire dec_4x16_1_b0, dec_4x16_1_b1, dec_4x16_1_b2, dec_4x16_1_b3, dec_4x16_1_b4, dec_4x16_1_b5,
       dec_4x16_1_b6, dec_4x16_1_b7, dec_4x16_1_b8, dec_4x16_1_b9, dec_4x16_1_b10, dec_4x16_1_b11,
       dec_4x16_1_b12, dec_4x16_1_b13, dec_4x16_1_b14, dec_4x16_1_b15;
  wire [7:0] memory_byte_1_q, memory_byte_2_q, memory_byte_3_q, memory_byte_4_q, memory_byte_5_q,
       memory_byte_6_q, memory_byte_7_q, memory_byte_8_q, memory_byte_9_q, memory_byte_10_q,
       memory_byte_11_q, memory_byte_12_q, memory_byte_13_q, memory_byte_14_q, memory_byte_15_q,
       memory_byte_16_q;

  Dec_4x16 dec_4x16_1 (
    .D(S), .B0(dec_4x16_1_b0), .B1(dec_4x16_1_b1), .B2(dec_4x16_1_b2), .B3(dec_4x16_1_b3),
    .B4(dec_4x16_1_b4), .B5(dec_4x16_1_b5), .B6(dec_4x16_1_b6), .B7(dec_4x16_1_b7), .B8(dec_4x16_1_b8),
    .B9(dec_4x16_1_b9), .B10(dec_4x16_1_b10), .B11(dec_4x16_1_b11), .B12(dec_4x16_1_b12),
    .B13(dec_4x16_1_b13), .B14(dec_4x16_1_b14), .B15(dec_4x16_1_b15));
  Memory_Byte memory_byte_1 (.R_W(R_W), .D(D), .S(dec_4x16_1_b0), .Q(memory_byte_1_q));
  Memory_Byte memory_byte_2 (.R_W(R_W), .D(D), .S(dec_4x16_1_b2), .Q(memory_byte_2_q));
  Memory_Byte memory_byte_3 (.R_W(R_W), .D(D), .S(dec_4x16_1_b4), .Q(memory_byte_3_q));
  Memory_Byte memory_byte_4 (.R_W(R_W), .D(D), .S(dec_4x16_1_b6), .Q(memory_byte_4_q));
  Memory_Byte memory_byte_5 (.R_W(R_W), .D(D), .S(dec_4x16_1_b8), .Q(memory_byte_5_q));
  Memory_Byte memory_byte_6 (.R_W(R_W), .D(D), .S(dec_4x16_1_b10), .Q(memory_byte_6_q));
  Memory_Byte memory_byte_7 (.R_W(R_W), .D(D), .S(dec_4x16_1_b12), .Q(memory_byte_7_q));
  Memory_Byte memory_byte_8 (.R_W(R_W), .D(D), .S(dec_4x16_1_b14), .Q(memory_byte_8_q));
  Memory_Byte memory_byte_9 (.R_W(R_W), .D(D), .S(dec_4x16_1_b1), .Q(memory_byte_9_q));
  Memory_Byte memory_byte_10 (.R_W(R_W), .D(D), .S(dec_4x16_1_b3), .Q(memory_byte_10_q));
  Memory_Byte memory_byte_11 (.R_W(R_W), .D(D), .S(dec_4x16_1_b5), .Q(memory_byte_11_q));
  Memory_Byte memory_byte_12 (.R_W(R_W), .D(D), .S(dec_4x16_1_b7), .Q(memory_byte_12_q));
  Memory_Byte memory_byte_13 (.R_W(R_W), .D(D), .S(dec_4x16_1_b9), .Q(memory_byte_13_q));
  Memory_Byte memory_byte_14 (.R_W(R_W), .D(D), .S(dec_4x16_1_b11), .Q(memory_byte_14_q));
  Memory_Byte memory_byte_15 (.R_W(R_W), .D(D), .S(dec_4x16_1_b13), .Q(memory_byte_15_q));
  Memory_Byte memory_byte_16 (.R_W(R_W), .D(D), .S(dec_4x16_1_b15), .Q(memory_byte_16_q));
  Or_Inator_16x1_8_Bit or_inator_16x1_8_bit_1 (
    .D0(memory_byte_1_q), .D1(memory_byte_9_q), .D2(memory_byte_2_q), .D3(memory_byte_10_q),
    .D4(memory_byte_3_q), .D5(memory_byte_11_q), .D6(memory_byte_4_q), .D7(memory_byte_12_q),
    .D8(memory_byte_5_q), .D9(memory_byte_13_q), .D10(memory_byte_6_q), .D11(memory_byte_14_q),
    .D12(memory_byte_7_q), .D13(memory_byte_15_q), .D14(memory_byte_8_q), .D15(memory_byte_16_q), .Q(Q));
endmodule

module Memory_Byte (
  input  R_W,
  input  [7:0] D,
  input  S,
  output [7:0] Q
);

  Memory_Cell memory_cell_1 (.R_W(R_W), .D(D[0]), .S(S), .Q(Q[0]));
  Memory_Cell memory_cell_2 (.R_W(R_W), .D(D[4]), .S(S), .Q(Q[4]));
  Memory_Cell memory_cell_3 (.R_W(R_W), .D(D[1]), .S(S), .Q(Q[1]));
  Memory_Cell memory_cell_4 (.R_W(R_W), .D(D[5]), .S(S), .Q(Q[5]));
  Memory_Cell memory_cell_5 (.R_W(R_W), .D(D[2]), .S(S), .Q(Q[2]));
  Memory_Cell memory_cell_6 (.R_W(R_W), .D(D[6]), .S(S), .Q(Q[6]));
  Memory_Cell memory_cell_7 (.R_W(R_W), .D(D[3]), .S(S), .Q(Q[3]));
  Memory_Cell memory_cell_8 (.R_W(R_W), .D(D[7]), .S(S), .Q(Q[7]));
endmodule

module Or_Inator_2x1_8_Bit (
  input  [7:0] D0,
  input  [7:0] D1,
  output [7:0] Q
);

  or or_1 (Q[0], D0[0], D1[0]);
  or or_2 (Q[1], D0[1], D1[1]);
  or or_3 (Q[2], D0[2], D1[2]);
  or or_4 (Q[3], D0[3], D1[3]);
  or or_5 (Q[4], D0[4], D1[4]);
  or or_6 (Q[5], D0[5], D1[5]);
  or or_7 (Q[6], D0[6], D1[6]);
  or or_8 (Q[7], D0[7], D1[7]);
endmodule

module Or_Inator_16x1_8_Bit (
  input  [7:0] D0,
  input  [7:0] D1,
  input  [7:0] D2,
  input  [7:0] D3,
  input  [7:0] D4,
  input  [7:0] D5,
  input  [7:0] D6,
  input  [7:0] D7,
  input  [7:0] D8,
  input  [7:0] D9,
  input  [7:0] D10,
  input  [7:0] D11,
  input  [7:0] D12,
  input  [7:0] D13,
  input  [7:0] D14,
  input  [7:0] D15,
  output [7:0] Q
);

  wire [7:0] or_inator_2x1_8_bit_1_q, or_inator_2x1_8_bit_2_q, or_inator_2x1_8_bit_3_q,
       or_inator_2x1_8_bit_4_q, or_inator_2x1_8_bit_5_q, or_inator_2x1_8_bit_6_q, or_inator_2x1_8_bit_7_q,
       or_inator_2x1_8_bit_8_q, or_inator_2x1_8_bit_9_q, or_inator_2x1_8_bit_10_q, or_inator_2x1_8_bit_11_q,
       or_inator_2x1_8_bit_12_q, or_inator_2x1_8_bit_13_q, or_inator_2x1_8_bit_14_q;

  Or_Inator_2x1_8_Bit or_inator_2x1_8_bit_1 (.D0(D0), .D1(D1), .Q(or_inator_2x1_8_bit_1_q));
  Or_Inator_2x1_8_Bit or_inator_2x1_8_bit_2 (.D0(D2), .D1(D3), .Q(or_inator_2x1_8_bit_2_q));
  Or_Inator_2x1_8_Bit or_inator_2x1_8_bit_3 (.D0(D4), .D1(D5), .Q(or_inator_2x1_8_bit_3_q));
  Or_Inator_2x1_8_Bit or_inator_2x1_8_bit_4 (.D0(D6), .D1(D7), .Q(or_inator_2x1_8_bit_4_q));
  Or_Inator_2x1_8_Bit or_inator_2x1_8_bit_5 (.D0(D8), .D1(D9), .Q(or_inator_2x1_8_bit_5_q));
  Or_Inator_2x1_8_Bit or_inator_2x1_8_bit_6 (.D0(D10), .D1(D11), .Q(or_inator_2x1_8_bit_6_q));
  Or_Inator_2x1_8_Bit or_inator_2x1_8_bit_7 (.D0(D12), .D1(D13), .Q(or_inator_2x1_8_bit_7_q));
  Or_Inator_2x1_8_Bit or_inator_2x1_8_bit_8 (.D0(D14), .D1(D15), .Q(or_inator_2x1_8_bit_8_q));
  Or_Inator_2x1_8_Bit or_inator_2x1_8_bit_9 (
    .D0(or_inator_2x1_8_bit_1_q), .D1(or_inator_2x1_8_bit_2_q), .Q(or_inator_2x1_8_bit_9_q));
  Or_Inator_2x1_8_Bit or_inator_2x1_8_bit_10 (
    .D0(or_inator_2x1_8_bit_3_q), .D1(or_inator_2x1_8_bit_4_q), .Q(or_inator_2x1_8_bit_10_q));
  Or_Inator_2x1_8_Bit or_inator_2x1_8_bit_11 (
    .D0(or_inator_2x1_8_bit_5_q), .D1(or_inator_2x1_8_bit_6_q), .Q(or_inator_2x1_8_bit_11_q));
  Or_Inator_2x1_8_Bit or_inator_2x1_8_bit_12 (
    .D0(or_inator_2x1_8_bit_7_q), .D1(or_inator_2x1_8_bit_8_q), .Q(or_inator_2x1_8_bit_12_q));
  Or_Inator_2x1_8_Bit or_inator_2x1_8_bit_13 (
    .D0(or_inator_2x1_8_bit_9_q), .D1(or_inator_2x1_8_bit_10_q), .Q(or_inator_2x1_8_bit_13_q));
  Or_Inator_2x1_8_Bit or_inator_2x1_8_bit_14 (
    .D0(or_inator_2x1_8_bit_11_q), .D1(or_inator_2x1_8_bit_12_q), .Q(or_inator_2x1_8_bit_14_q));
  Or_Inator_2x1_8_Bit or_inator_2x1_8_bit_15 (.D0(or_inator_2x1_8_bit_13_q), .D1(or_inator_2x1_8_bit_14_q), .Q(Q));
endmodule

module CLU (
  input  q1,
  input  q2,
  input  q3,
  input  q4,
  input  q5,
  input  q7,
  input  [3:0] t,
  output x1,
  output x2,
  output x3,
  output x4,
  output x5,
  output x6,
  output x7,
  output x8,
  output [1:0] x9,
  output [1:0] x10,
  output [1:0] x11,
  output x12,
  output x13
);

  wire add_i_1_x2, add_i_1_x4_1, add_i_1_x6, add_i_1_x8, add_i_1_x9_01, add_i_1_x9_10, add_i_1_x11_11,
       add_i_1_x12, dec_4x16_1_b0, dec_4x16_1_b3, dec_4x16_1_b4, dec_4x16_1_b5, dec_4x16_1_b6, dec_4x16_1_b7,
       dec_4x16_1_b8, dec_4x16_1_b9, dec_4x16_1_b10, dec_4x16_1_b11, jmp_1_x6, jmp_1_x8_1, jmp_1_x8_2,
       jmp_1_x9_01, jmp_1_x9_10, jmp_1_x11_01, jmp_1_x11_10, jmp_1_x11_11, jmp_1_x12_1, jmp_1_x12_2,
       jmp_1_x12_3, lda_1_x2, lda_1_x4, lda_1_x6, lda_1_x12, ldi_1_x2_1, ldi_1_x2_2, ldi_1_x4_1, ldi_1_x4_2,
       ldi_1_x6, ldi_1_x10_10, ldi_1_x12, not_1_out, not_2_out, not_3_out, or_1_out, or_2_out, or_3_out,
       or_4_out, or_5_out, or_9_out, or_10_out, or_11_out, or_12_out, or_14_out, or_15_out, sta_1_x3,
       sta_1_x4, sta_1_x5, sta_1_x6, sta_1_x7, sti_1_x2_1, sti_1_x2_2, sti_1_x4_1, sti_1_x4_2, sti_1_x5,
       sti_1_x6, sti_1_x7, sti_1_x10_10;

  Dec_4x16 dec_4x16_1 (
    .D(t), .B0(dec_4x16_1_b0), .B1(x13), .B2(x1), .B3(dec_4x16_1_b3), .B4(dec_4x16_1_b4), .B5(dec_4x16_1_b5),
    .B6(dec_4x16_1_b6), .B7(dec_4x16_1_b7), .B8(dec_4x16_1_b8), .B9(dec_4x16_1_b9), .B10(dec_4x16_1_b10),
    .B11(dec_4x16_1_b11));  // open: B12, B13, B14, B15
  LDA lda_1 (
    .q1(q1), .t3(dec_4x16_1_b3), .t4(dec_4x16_1_b4), .t5(dec_4x16_1_b5), .t6(dec_4x16_1_b6), .x4(lda_1_x4),
    .x2(lda_1_x2), .x12(lda_1_x12), .x6(lda_1_x6));
  LDI ldi_1 (
    .q2(q2), .t3(dec_4x16_1_b3), .t4(dec_4x16_1_b4), .t5(dec_4x16_1_b5), .t6(dec_4x16_1_b6),
    .t7(dec_4x16_1_b7), .t8(dec_4x16_1_b8), .x4_1(ldi_1_x4_1), .x2_1(ldi_1_x2_1), .x10_10(ldi_1_x10_10),
    .x4_2(ldi_1_x4_2), .x2_2(ldi_1_x2_2), .x12(ldi_1_x12), .x6(ldi_1_x6));
  STA sta_1 (
    .q3(q3), .t3(dec_4x16_1_b3), .t4(dec_4x16_1_b4), .t5(dec_4x16_1_b5), .t6(dec_4x16_1_b6), .x7(sta_1_x7),
    .x3(sta_1_x3), .x4(sta_1_x4), .x5(sta_1_x5), .x6(sta_1_x6));
  STI sti_1 (
    .q4(q4), .t3(dec_4x16_1_b3), .t4(dec_4x16_1_b4), .t5(dec_4x16_1_b5), .t6(dec_4x16_1_b6),
    .t7(dec_4x16_1_b7), .t8(dec_4x16_1_b8), .x4_1(sti_1_x4_1), .x2_1(sti_1_x2_1), .x10_10(sti_1_x10_10),
    .x4_2(sti_1_x4_2), .x7(sti_1_x7), .x2_2(sti_1_x2_2), .x5(sti_1_x5), .x6(sti_1_x6));
  ADD_I add_i_1 (
    .q5(q5), .t3(dec_4x16_1_b3), .t4(dec_4x16_1_b4), .t5(dec_4x16_1_b5), .t6(dec_4x16_1_b6),
    .t7(dec_4x16_1_b7), .t8(dec_4x16_1_b8), .x4_1(add_i_1_x4_1), .x2(add_i_1_x2), .x9_01(add_i_1_x9_01),
    .x8(add_i_1_x8), .x9_10(add_i_1_x9_10), .x11_11(add_i_1_x11_11), .x12(add_i_1_x12), .x6(add_i_1_x6));
  JMP jmp_1 (
    .q7(q7), .t3(dec_4x16_1_b3), .t4(dec_4x16_1_b4), .t5(dec_4x16_1_b5), .t6(dec_4x16_1_b6),
    .t7(dec_4x16_1_b7), .t8(dec_4x16_1_b8), .t9(dec_4x16_1_b9), .x11_10(jmp_1_x11_10), .x12_1(jmp_1_x12_1),
    .x8_1(jmp_1_x8_1), .x9_01(jmp_1_x9_01), .x11_01(jmp_1_x11_01), .x12_2(jmp_1_x12_2), .x8_2(jmp_1_x8_2),
    .x9_10(jmp_1_x9_10), .x11_11(jmp_1_x11_11), .x12_3(jmp_1_x12_3), .x3(x3), .x6(jmp_1_x6));
  or or_1 (or_1_out, x13, add_i_1_x2);
  or or_2 (or_2_out, jmp_1_x8_1, jmp_1_x8_2);
  or or_3 (or_3_out, sti_1_x2_1, sti_1_x2_2, or_1_out);
  or or_4 (or_4_out, add_i_1_x4_1, sti_1_x4_2);
  or or_5 (or_5_out, sti_1_x5, sta_1_x5);
  or or_6 (x9[0], jmp_1_x9_01, add_i_1_x9_01);
  or or_7 (x9[1], add_i_1_x9_10, jmp_1_x9_10);
  or or_8 (x10[1], sti_1_x10_10, ldi_1_x10_10);
  or or_9 (or_9_out, ldi_1_x2_2, sta_1_x3, or_3_out);
  or or_10 (or_10_out, ldi_1_x4_2, sta_1_x4, sti_1_x4_1, or_4_out);
  not not_1 (not_1_out, or_5_out);
  not not_2 (not_2_out, not_1_out);
  or or_11 (or_11_out, sta_1_x6, sti_1_x6, jmp_1_x6);
  or or_12 (or_12_out, dec_4x16_1_b0, x10[1]);
  or or_13 (x11[1], add_i_1_x11_11, jmp_1_x11_11, jmp_1_x11_10);
  or or_14 (or_14_out, add_i_1_x12, jmp_1_x12_1, or_15_out);
  or or_15 (or_15_out, jmp_1_x12_2, jmp_1_x12_3);
  or or_16 (x2, ldi_1_x2_1, lda_1_x2, or_9_out);
  or or_17 (x4, dec_4x16_1_b0, lda_1_x4, ldi_1_x4_1, or_10_out);
  not not_3 (not_3_out, not_2_out);
  and and_1 (x5, not_3_out, or_5_out);
  or or_18 (x6, lda_1_x6, ldi_1_x6, or_11_out);
  or or_19 (x7, sta_1_x7, sti_1_x7);
  or or_20 (x8, add_i_1_x8, or_2_out, add_i_1_x6);
  not not_4 (x10[0], or_12_out);
  or or_21 (x11[0], jmp_1_x11_01, jmp_1_x11_11, add_i_1_x11_11);
  or or_22 (x12, lda_1_x12, ldi_1_x12, or_14_out);
endmodule

module Or_Inator_2x1_2_Bit (
  input  [1:0] D0,
  input  [1:0] D1,
  output [1:0] Q
);

  or or_1 (Q[0], D0[0], D1[0]);
  or or_2 (Q[1], D0[1], D1[1]);
endmodule

module LDA (
  input  q1,
  input  t3,
  input  t4,
  input  t5,
  input  t6,
  output x4,
  output x2,
  output x12,
  output x6
);

  and and_1 (x4, t3, q1);
  and and_2 (x2, t4, q1);
  and and_3 (x12, t5, q1);
  and and_4 (x6, t6, q1);
endmodule

module LDI (
  input  q2,
  input  t3,
  input  t4,
  input  t5,
  input  t6,
  input  t7,
  input  t8,
  output x4_1,
  output x2_1,
  output x10_10,
  output x4_2,
  output x2_2,
  output x12,
  output x6
);

  and and_1 (x4_1, t3, q2);
  and and_2 (x2_1, t4, q2);
  and and_3 (x4_2, t5, q2);
  and and_4 (x2_2, t6, q2);
  and and_5 (x12, t7, q2);
  and and_6 (x6, t8, q2);

  assign x10_10 = x4_2;
endmodule

module STA (
  input  q3,
  input  t3,
  input  t4,
  input  t5,
  input  t6,
  output x7,
  output x3,
  output x4,
  output x5,
  output x6
);

  and and_1 (x3, t3, q3);
  and and_2 (x4, t4, q3);
  and and_3 (x5, t5, q3);
  and and_4 (x6, t6, q3);

  assign x7 = x3;
endmodule

module STI (
  input  q4,
  input  t3,
  input  t4,
  input  t5,
  input  t6,
  input  t7,
  input  t8,
  output x4_1,
  output x2_1,
  output x10_10,
  output x4_2,
  output x7,
  output x2_2,
  output x5,
  output x6
);

  and and_1 (x4_1, t3, q4);
  and and_2 (x2_1, t4, q4);
  and and_3 (x4_2, t5, q4);
  and and_4 (x2_2, t6, q4);
  and and_5 (x5, t7, q4);
  buf and_6 (x6, t8);  // AND_Gate

  assign x7 = x2_2;
  assign x10_10 = x4_2;
endmodule

module ADD_I (
  input  q5,
  input  t3,
  input  t4,
  input  t5,
  input  t6,
  input  t7,
  input  t8,
  output x4_1,
  output x2,
  output x9_01,
  output x8,
  output x9_10,
  output x11_11,
  output x12,
  output x6
);

  and and_1 (x4_1, t3, q5);
  and and_2 (x2, t4, q5);
  and and_3 (x9_01, t5, q5);
  and and_4 (x8, t6, q5);
  and and_5 (x11_11, t7, q5);
  and and_6 (x6, t8, q5);

  assign x9_10 = x8;
  assign x12 = x11_11;
endmodule

module JMP (
  input  q7,
  input  t3,
  input  t4,
  input  t5,
  input  t6,
  input  t7,
  input  t8,
  input  t9,
  output x11_10,
  output x12_1,
  output x8_1,
  output x9_01,
  output x11_01,
  output x12_2,
  output x8_2,
  output x9_10,
  output x11_11,
  output x12_3,
  output x3,
  output x6
);

  and and_1 (x11_10, t3, q7);
  and and_2 (x8_1, t4, q7);
  and and_3 (x11_01, t5, q7);
  and and_4 (x8_2, t6, q7);
  and and_5 (x11_11, t7, q7);
  and and_6 (x3, t8, q7);
  and and_7 (x6, t9, q7);

  assign x9_01 = x8_1;
  assign x9_10 = x8_2;
  assign x12_1 = x11_10;
  assign x12_2 = x11_01;
  assign x12_3 = x11_11;
endmodule

module PC (
  input  [3:0] D,
  input  LOAD,
  input  INC,
  output [3:0] Q
);

  wire and_1_out, not_1_out, not_2_out, not_3_out, or_1_out;
  wire [3:0] add_4_bit_1_sum, mplxr_2x1_4_bit_1_out_4, register_4_bit_1_q, register_4_bit_2_q;

  not not_1 (not_1_out, INC);
  not not_2 (not_2_out, not_1_out);
  and and_1 (and_1_out, INC, not_3_out);
  not not_3 (not_3_out, not_2_out);
  Add_4_Bit add_4_bit_1 (.A(Q), .B(4'b0001), .SUM(add_4_bit_1_sum));  // open: C_IN, C_OUT
  Register_4_Bit register_4_bit_1 (.D(D), .LOAD(LOAD), .Q(register_4_bit_1_q));
  Register_4_Bit register_4_bit_2 (.D(add_4_bit_1_sum), .LOAD(and_1_out), .Q(register_4_bit_2_q));
  Mplxr_2x1_4_Bit mplxr_2x1_4_bit_1 (
    .D0(register_4_bit_1_q), .D1(register_4_bit_2_q), .S(INC), .out_4(mplxr_2x1_4_bit_1_out_4));
  or or_1 (or_1_out, LOAD, INC);
  Register_4_Bit register_4_bit_3 (.D(mplxr_2x1_4_bit_1_out_4), .LOAD(or_1_out), .Q(Q));
endmodule

module ALU (
  input  [7:0] D,
  input  [1:0] LOAF,
  output [7:0] out_3
);

  wire and_1_out, not_1_out, not_2_out, not_3_out, or_1_out;
  wire [7:0] add_8_bit_1_sum, mplxr_2x1_8_bit_1_q, register_8_bit_1_q;

  Add_8_Bit add_8_bit_1 (.A(D), .B(out_3), .SUM(add_8_bit_1_sum));  // open: C_IN, C_OUT
  not not_1 (not_1_out, LOAF[1]);
  Mplxr_2x1_8_Bit mplxr_2x1_8_bit_1 (.D0(D), .D1(register_8_bit_1_q), .S(LOAF[1]), .Q(mplxr_2x1_8_bit_1_q));
  not not_2 (not_2_out, not_1_out);
  not not_3 (not_3_out, not_2_out);
  or or_1 (or_1_out, LOAF[0], LOAF[1]);
  and and_1 (and_1_out, LOAF[1], not_3_out);
  Register_8_Bit register_8_bit_1 (.D(add_8_bit_1_sum), .LOAD(and_1_out), .Q(register_8_bit_1_q));
  Register_8_Bit register_8_bit_2 (.D(mplxr_2x1_8_bit_1_q), .LOAD(or_1_out), .Q(out_3));
endmodule

module Drop_4 (
  input  [7:0] D,
  output [3:0] Q
);


  assign Q = D[3:0];
endmodule

module Add_4 (
  input  [3:0] D,
  output [7:0] Q
);


  assign Q = {4'b0000, D};
endmodule
